# Fritzing sketch ControlBox (saved by Fritzing 0.9.3b)
circuit board: 10cm x 8cm

parts:
  Teensy_3_1 = Teensy 3.1
  POT1 = Rotary Potentiometer (Small) [maximum_resistance=10kΩ package=THT]
  SPOT1 = Slide Potentiometer [maximum_resistance=10kΩ]
  SPOT2 = Slide Potentiometer [maximum_resistance=10kΩ]
  POT2 = Rotary Potentiometer (Small) [maximum_resistance=10kΩ package=THT]
  POT3 = Rotary Potentiometer (Small) [maximum_resistance=10kΩ package=THT]
  POT8 = Rotary Potentiometer (Small) [maximum_resistance=10kΩ package=THT]
  POT9 = Rotary Potentiometer (Small) [maximum_resistance=10kΩ package=THT]
  POT5 = Rotary Potentiometer (Small) [maximum_resistance=10kΩ package=THT]
  POT7 = Rotary Potentiometer (Small) [maximum_resistance=10kΩ package=THT]
  POT4 = Rotary Potentiometer (Small) [maximum_resistance=10kΩ package=THT]
  POT6 = Rotary Potentiometer (Small) [maximum_resistance=10kΩ package=THT]
  SPKR1 = Loudspeaker
  LED1 = LED - 5mm [color="Blue (525nm)" package="5 mm [THT]"]
  S1 = Pushbutton [package="[THT]"]
  S2 = Pushbutton [package="[THT]"]
  S3 = Pushbutton [package="[THT]"]
  S4 = Pushbutton [package="[THT]"]
  S5 = Pushbutton [package="[THT]"]
  S6 = Pushbutton [package="[THT]"]
  S7 = Pushbutton [package="[THT]"]
  S8 = Pushbutton [package="[THT]"]
  LED2 = LED - 5mm [color="Red (633nm)" package="5 mm [THT]"]
  S9 = Pushbutton [package="[THT]"]
  IC1 = Voltage Regulator AMS1117 [package=sot223]

nets:
  GND: Teensy_3_1.GND, Teensy_3_1.AGND, POT1.leg2, SPOT1.leg2, SPOT2.leg2, POT2.leg2, POT3.leg2, POT8.leg2, POT9.leg2, POT5.leg2, POT7.leg2, POT4.leg2, POT6.leg2, SPKR1.pin1, LED1.cathode, S1.Pin_1, S1.Pin_2, S2.Pin_1, S2.Pin_2, S3.Pin_1, S3.Pin_2, S4.Pin_1, S4.Pin_2, S5.Pin_1, S5.Pin_2, S6.Pin_1, S6.Pin_2, S7.Pin_1, S7.Pin_2, S8.Pin_1, S8.Pin_2, LED2.cathode, S9.Pin_1, S9.Pin_2, IC1.GND
  N1: Teensy_3_1.D2, S1.Pin_3, S1.Pin_4
  N2: Teensy_3_1.D3, S2.Pin_3, S2.Pin_4
  N3: Teensy_3_1.D4, S3.Pin_3, S3.Pin_4
  N4: Teensy_3_1.D5, S4.Pin_3, S4.Pin_4
  N5: Teensy_3_1.D6, S5.Pin_3, S5.Pin_4
  N6: Teensy_3_1.D7, S6.Pin_3, S6.Pin_4
  N7: Teensy_3_1.D8, S7.Pin_3, S7.Pin_4
  N8: Teensy_3_1.D9, S8.Pin_3, S8.Pin_4
  N9: Teensy_3_1.D10, S9.Pin_3, S9.Pin_4
  N10: Teensy_3_1.A14/DAC, SPKR1.pin2
  N11: Teensy_3_1.D13, LED1.anode
  N12: Teensy_3_1.A0/D14, SPOT1.wiper
  N13: Teensy_3_1.A1/D15, SPOT2.wiper
  N14: Teensy_3_1.A2/D16, POT1.wiper
  N15: Teensy_3_1.A3/D17, POT2.wiper
  N16: Teensy_3_1.A4/D18, POT3.wiper
  N17: Teensy_3_1.A5/D19, POT4.wiper
  N18: Teensy_3_1.A6/D20, POT5.wiper
  N19: Teensy_3_1.A7/D21, POT6.wiper
  N20: Teensy_3_1.A8/D22, POT7.wiper
  N21: Teensy_3_1.A9/D23, POT8.wiper
  N22: Teensy_3_1.3V3, Teensy_3_1.AREF, POT1.leg1, SPOT1.leg1, SPOT2.leg1, POT2.leg1, POT3.leg1, POT8.leg1, POT9.leg1, POT5.leg1, POT7.leg1, POT4.leg1, POT6.leg1, LED2.anode, IC1.OUT
  N23: Teensy_3_1.Vin, Teensy_3_1.VUSB, IC1.IN
  N24: Teensy_3_1.A10, POT9.wiper
