# Fritzing sketch SFX_Btn (saved by Fritzing 0.9.3b)
circuit board: 8.46667cm x 5.64444cm

parts:
  Teensy_3_1 = Teensy 3.1
  S1 = Pushbutton [package="[THT]"]
  S2 = Pushbutton [package="[THT]"]
  S3 = Pushbutton [package="[THT]"]
  S4 = Pushbutton [package="[THT]"]
  S5 = Pushbutton [package="[THT]"]
  S6 = Pushbutton [package="[THT]"]
  S7 = Pushbutton [package="[THT]"]
  S8 = Pushbutton [package="[THT]"]
  S9 = Pushbutton [package="[THT]"]
  S10 = Pushbutton [package="[THT]"]
  S11 = Pushbutton [package="[THT]"]
  S12 = Pushbutton [package="[THT]"]
  S13 = Pushbutton [package="[THT]"]
  S14 = Pushbutton [package="[THT]"]
  S15 = Pushbutton [package="[THT]"]
  S16 = Pushbutton [package="[THT]"]
  S17 = Pushbutton [package="[THT]"]
  S18 = Pushbutton [package="[THT]"]

nets:
  N1: Teensy_3_1.GND, Teensy_3_1.AGND, S1.Pin_3, S1.Pin_4, S2.Pin_3, S2.Pin_4, S3.Pin_3, S3.Pin_4, S4.Pin_3, S4.Pin_4, S5.Pin_3, S5.Pin_4, S6.Pin_3, S6.Pin_4, S7.Pin_3, S7.Pin_4, S8.Pin_3, S8.Pin_4, S9.Pin_3, S9.Pin_4, S10.Pin_3, S10.Pin_4, S11.Pin_3, S11.Pin_4, S12.Pin_3, S12.Pin_4, S13.Pin_3, S13.Pin_4, S14.Pin_3, S14.Pin_4, S15.Pin_3, S15.Pin_4, S16.Pin_3, S16.Pin_4, S17.Pin_3, S17.Pin_4, S18.Pin_3, S18.Pin_4
  N2: Teensy_3_1.D2, S1.Pin_1, S1.Pin_2
  N3: Teensy_3_1.D3, S2.Pin_1, S2.Pin_2
  N4: Teensy_3_1.D4, S3.Pin_1, S3.Pin_2
  N5: Teensy_3_1.D5, S4.Pin_1, S4.Pin_2
  N6: Teensy_3_1.D6, Teensy_3_1.D7, S5.Pin_1, S5.Pin_2
  N7: Teensy_3_1.D8, S6.Pin_1, S6.Pin_2
  N8: Teensy_3_1.D9, S7.Pin_1, S7.Pin_2
  N9: Teensy_3_1.D10, S8.Pin_1, S8.Pin_2
  N10: Teensy_3_1.D11, S9.Pin_1, S9.Pin_2
  N11: Teensy_3_1.D12, S10.Pin_1, S10.Pin_2
  N12: Teensy_3_1.A0/D14, S11.Pin_1, S11.Pin_2
  N13: Teensy_3_1.A1/D15, S12.Pin_1, S12.Pin_2
  N14: Teensy_3_1.A2/D16, S13.Pin_1, S13.Pin_2
  N15: Teensy_3_1.A3/D17, S14.Pin_1, S14.Pin_2
  N16: Teensy_3_1.A4/D18, S15.Pin_1, S15.Pin_2
  N17: Teensy_3_1.A5/D19, S16.Pin_1, S16.Pin_2
  N18: Teensy_3_1.A6/D20, S17.Pin_1, S17.Pin_2
  N19: Teensy_3_1.A7/D21, S18.Pin_1, S18.Pin_2

notes:
  MIDI SFX Buttons
